# Fritzing sketch Plasma CNC (saved by Fritzing 0.9.2b)
breadboards: 1

parts:
  Power_plug1 = Power plug
  Fuse1 = Fuse with Handler [part_number=Htc-15m]
  M1 = Stepper Motor - Bipolar
  MD09B1 = A4988 Stepper Motor Driver Carrier
  MD09B2 = A4988 Stepper Motor Driver Carrier
  Part1 = Arduino Uno (Rev3)
  S1 = Pushbutton [package="[THT]"]
  S2 = Pushbutton [package="[THT]"]
  S3 = Round Pushbutton
  C3 = Electrolytic Capacitor [capacitance=100µF voltage=35V package="100 mil [THT, electrolytic]"]
  U1 = Voltage Regulator - 5V [package="TO220 [THT]"]
  S4 = Round Pushbutton
  U3 = RELAY [package=relay-g5q]
  M3 = DC Motor
  M2 = Stepper Motor - Bipolar

nets:
  GND: Power_plug1.GND, MD09B1.GROUND, MD09B2.GROUND, Part1.GND, S1.Pin_1, S1.Pin_2, S2.Pin_1, S2.Pin_2, S3.leg1, C3.-, U1.GND, S4.leg1, U3.COIL2, M3.pin_1
  N1: Power_plug1.VCC, Fuse1.Connector2
  N2: Fuse1.Connector1, MD09B1.VMOT, MD09B2.VMOT, C3.+, U1.input_voltage, M3.pin_2
  N3: M1.A, MD09B1.OUT_2B
  N4: M1.C, MD09B1.OUT_2A
  N5: M1.B, MD09B1.OUT_1A
  N6: M1.D, MD09B1.OUT_1B
  N7: MD09B1.Enable, MD09B2.Enable, Part1.D8
  N8: MD09B1.RESET, MD09B1.SLEEP
  N9: MD09B1.STEP, Part1.D2
  N10: MD09B1.DIR, Part1.D5_PWM
  VDD: MD09B1.VDD, MD09B2.VDD, Part1.VIN, U1.output_voltage
  N11: MD09B2.RESET, MD09B2.SLEEP
  N12: MD09B2.STEP, Part1.D3_PWM
  N13: MD09B2.DIR, Part1.D6_PWM
  N14: MD09B2.OUT_2B, M2.A
  N15: MD09B2.OUT_2A, M2.C
  N16: MD09B2.OUT_1A, M2.B
  N17: MD09B2.OUT_1B, M2.D
  N18: Part1.A0, S3.leg0
  N19: Part1.A2, S4.leg0
  N20: Part1.D9_PWM, S2.Pin_3, S2.Pin_4
  N21: Part1.D10_PWM/SS, S1.Pin_3
  N22: Part1.D11_PWM/MOSI, U3.NO

notes:
  5V VREG Circuit
  X
  Y
  Emergency Stop
  5V Rail
  HV Rail
  Cycle Start
  Plasma Gun Switch
  To Gun
  Y Endstop
  X Endstop
  Cooling Fan
  CNC Controller Board
  GCode Interpreter
